# Fritzing sketch QuickEyesFastHands_feather (saved by Fritzing 0.9.4)
breadboards: 2

parts:
  8_Channel_Relay1 = 8 Channel Power Relay
  Part2 = Adafruit Feather M0 Basic Proto [part_number="Adafruit #2772"]
  S1 = Round Pushbutton
  J1 = Power Jack [package=power_jack_pth]
  L1 = Solenoid
  L2 = Solenoid
  L3 = Solenoid
  L4 = Solenoid
  L5 = Solenoid
  L6 = Solenoid
  L7 = Solenoid
  L8 = Solenoid

nets:
  GND: 8_Channel_Relay1.GND, 8_Channel_Relay1.COM#22, 8_Channel_Relay1.COM#25, 8_Channel_Relay1.COM#28, 8_Channel_Relay1.COM#31, 8_Channel_Relay1.COM#34, 8_Channel_Relay1.COM#37, 8_Channel_Relay1.COM#40, Part2.GND, S1.leg1, J1.GND
  N1: 8_Channel_Relay1.IN1, Part2.A3
  N2: 8_Channel_Relay1.IN2, Part2.A2
  N3: 8_Channel_Relay1.IN3, Part2.A1
  N4: 8_Channel_Relay1.IN4, Part2.A0
  N5: 8_Channel_Relay1.IN5, Part2.D6
  N6: 8_Channel_Relay1.IN6, Part2.D9
  N7: 8_Channel_Relay1.IN7, Part2.D10
  N8: 8_Channel_Relay1.IN8, Part2.D11
  N9: 8_Channel_Relay1.VCC, Part2.VBAT, J1.PWR, L1.pin2, L2.pin2, L3.pin2, L4.pin2, L5.pin2, L6.pin2, L7.pin2, L8.pin2
  N10: 8_Channel_Relay1.NC#21, L1.pin1
  N11: 8_Channel_Relay1.NC#24, L2.pin1
  N12: 8_Channel_Relay1.NC#27, L3.pin1
  N13: 8_Channel_Relay1.NC#30, L4.pin1
  N14: 8_Channel_Relay1.NC#33, L5.pin1
  N15: 8_Channel_Relay1.NC#36, L6.pin1
  N16: 8_Channel_Relay1.NC#39, L7.pin1
  N17: 8_Channel_Relay1.NC#42, L8.pin1
  N18: Part2.D5, S1.leg0

custom parts:
  8 Channel Power Relay: An 8 channel power relay. The module operates at 5V.
  Adafruit Feather M0 Basic Proto: At the Feather M0's heart is an ATSAMD21G18 ARM Cortex M0 processor, clocked at 48 MHz and at 3.3V logic, the same one used in the new Arduino Zero. This chip has a whopping 256K of FLASH (8x more than the Atmega328 or 32u4) and 32K of RAM (16x as much)! This chip comes with built in USB so it has USB-to-Serial program & debug capability built in with no need for an FTDI-like chip. To make it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
